# Fritzing sketch Ventilatore (saved by Fritzing 0.9.3b)
breadboards: 1

parts:
  Componente1 = Arduino Uno (Rev3)
  M1 = DC Motor
  D1 = Rectifier Diode [part_number=1N4001 package="300 mil [THT]"]
  Q1 = NPN-Transistor [package="TO92 [THT]"]
  R1 = Resistor [tolerance=±5% resistance=220 package=THT]
  C1 = Ceramic Capacitor [capacitance=100nF package="100 mil [THT, multilayer]"]
  R2 = Resistor [tolerance=±5% resistance=220 package=THT]

nets:
  N1: Componente1.A0, C1.1, R2.Pin_0
  N2: Componente1.D5_PWM, R1.Pin_1
  N3: M1.pin_1, D1.anode, C1.0
  N4: M1.pin_2, D1.cathode, Q1.E
  N5: Q1.B, R1.Pin_0
  N6: Q1.C, R2.Pin_1
